# Fritzing sketch skema keseluruhan (saved by Fritzing 1.0.6)

parts:
  J1 = STM32 Nucleo boards
  ZMPT101 = zmpt101b
  ACS712 = ACS712 Current Sensor 5A 20A 30A
  AC_IN = 220v plug
  LAMP2 = Incandescent light bulb small [package="bulb sm"]
  LAMP1 = Incandescent light bulb small [package="bulb sm"]
  LAMP3 = Incandescent light bulb small [package="bulb sm"]
  S1 = Pushbutton [package=THT]
  S2 = Pushbutton [package=THT]
  S3 = Pushbutton [package=THT]
  LCD_16X2 = LCD screen 16x2 IIC [part_number=101290]

nets:
  N1: J1.A0, ZMPT101.OUT
  N2: J1.A1, ZMPT101.L, ACS712.2, ACS712.OUT, S1.leg1, S2.leg1, S3.leg1
  N3: J1.A4/SDA, LCD_16X2.SDA
  N4: J1.A5/SCL, LCD_16X2.SCL
  VCC: J1.5V, ZMPT101.VCC, ACS712.VCC, LCD_16X2.VCC
  GND: J1.GND, ZMPT101.GND, ACS712.GND, LCD_16X2.GND
  N5: ZMPT101.N, AC_IN.pin2, LAMP2.2, LAMP1.2, LAMP3.2
  N6: ACS712.1, AC_IN.pin1
  N7: LAMP2.1, S2.leg0
  N8: LAMP1.1, S1.leg0
  N9: LAMP3.1, S3.leg0

custom parts:
  zmpt101b: Single phase ac active output voltate transformer module.
  ACS712 Current Sensor 5A 20A 30A: Remix by Michael Kubina http://www.kubina.info Original by: https://forum.fritzing.org/t/current-sensor-5a-acs712/7694 https://forum.fritzing.org/u/ArtHome ArtHome12@gmail.com
  220v plug: Generic 220V AC plug.
  LCD screen 16x2 IIC: LCD screen with HD44780 controller enables showing text, symbols, value or anything else that comes from Croduino/Arduino. It is capable of showing 16 symbols in two lines and therefore can be used in many projects that need to send clearly visible and legible output information.. • Color of symbols: White • Backlight: Blue • Dimensions: 80 x 36 x 12 mm • Screen dimensions: 64.5 x 16 mm •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
